// Logisim project breizhCHIP.circ as structural Verilog: 2 circuits, main circuit main
module main (
);

  wire clock_1_out, clock_2_out, clock_3_out;
  wire [1:0] adder_1_out, adder_2_out, register_1_q, register_2_q;
  wire [6:0] keyboard_1_data;
  wire [7:0] rom_1_data, rom_2_data, xor_1_out, xor_2_out;

  Register #(.width(2)) register_1 (.D(adder_1_out), .en(1'b1), .clk(clock_1_out), .Q(register_1_q), .clr(1'b0));
  Clock clock_1 (.out(clock_1_out));
  ROM #(.addrWidth(2)) rom_1 (.addr(register_1_q), .data(rom_1_data));
  Adder #(.width(2)) adder_1 (.a(register_1_q), .b(2'b01), .out(adder_1_out));  // open: cin, cout
  Clock clock_2 (.out(clock_2_out));
  Keyboard keyboard_1 (.clk(clock_2_out), .data(keyboard_1_data));  // open: re, clr, avail
  Register #(.width(2)) register_2 (.D(adder_2_out), .en(1'b1), .clk(clock_3_out), .Q(register_2_q), .clr(1'b0));
  Clock clock_3 (.out(clock_3_out));
  assign xor_1_out = rom_1_data ^ rom_2_data;  // XOR_Gate xor_1, 8 bits wide
  ROM #(.addrWidth(2)) rom_2 (.addr(register_2_q), .data(rom_2_data));
  assign xor_2_out = xor_1_out ^ {1'b0, keyboard_1_data};  // XOR_Gate xor_2, 8 bits wide
  Adder #(.width(2)) adder_2 (.a(register_2_q), .b({1'b0, register_1_q[0]}), .out(adder_2_out));  // open: cin, cout
  Hex_Digit_Display hex_digit_display_1 (.value(xor_2_out[7:4]));  // open: dp
  Hex_Digit_Display hex_digit_display_2 (.value(xor_2_out[3:0]));  // open: dp

  // Notes on the sheet:
  //   contents of rom_1 (hex, n*v repeats v):
  //   de ad be ef
  //   contents of rom_2 (hex, n*v repeats v):
  //   ca fe ba be
endmodule

module rotor (
  input  in_1,
  output out_2,
  output [7:0] out_3
);

  wire [1:0] adder_1_out;
  wire [1:1] register_1_q;

  Register #(.width(2)) register_1 (.D(adder_1_out), .en(1'b1), .clk(in_1), .Q({register_1_q[1], out_2}), .clr(1'b0));
  ROM #(.addrWidth(2)) rom_1 (.addr({register_1_q[1], out_2}), .data(out_3));
  Adder #(.width(2)) adder_1 (.a({register_1_q[1], out_2}), .b(2'b01), .out(adder_1_out));  // open: cin, cout

  // Notes on the sheet:
  //   contents of rom_1 (hex, n*v repeats v):
  //   de ad be ef
endmodule
